# Fritzing sketch FinalWork (saved by Fritzing 0.9.3b)
perfboards: 1

parts:
  元件1 = Analog Digital MUX Breakout
  元件2 = Analog Digital MUX Breakout
  U1 = 74HC595 [package="DIP16 [THT]"]
  U2 = 74HC595 [package="DIP16 [THT]"]
  S1 = Round Pushbutton  # not connected
  U3 = ENCODER-QUADRATURE [package=encoder-16mm-quad]  # not connected
  LED1 = LED - 3mm [color="Red (633nm)" package="3 mm [THT]"]  # not connected
  元件7 = Arduino Uno (Rev3)
  JP10 = Header 4 [package=1x04-1mm-ra]
  JP11 = Header 4 [package=1x04-1mm-ra]
  JP16 = Header 4 [package=1x04-1mm-ra]
  JP18 = Header 4 [package=1x04-1mm-ra]
  JP22 = Header 4 [package=1x04-1mm-ra]
  JP24 = Header 4 [package=1x04-1mm-ra]
  JP28 = Header 4 [package=1x04-1mm-ra]
  JP30 = Header 4 [package=1x04-1mm-ra]
  JP34 = Header 4 [package=1x04-1mm-ra]
  JP36 = Header 4 [package=1x04-1mm-ra]
  JP43 = Header 4 [package=1x04-1mm-ra]
  JP49 = Header 4 [package=1x04-1mm-ra]
  JP51 = Header 4 [package=1x04-1mm-ra]
  JP53 = Header 4 [package=1x04-1mm-ra]
  JP55 = Header 4 [package=1x04-1mm-ra]
  JP57 = Header 4 [package=1x04-1mm-ra]
  元件8 = Analog Digital MUX Breakout
  JP58 = Header 4 [package=1x04-1mm-ra]
  JP59 = Header 4 [package=1x04-1mm-ra]
  JP60 = Header 4 [package=1x04-1mm-ra]
  JP61 = Header 4 [package=1x04-1mm-ra]
  JP62 = Header 4 [package=1x04-1mm-ra]
  JP63 = Header 4 [package=1x04-1mm-ra]
  JP64 = Header 4 [package=1x04-1mm-ra]
  JP65 = Header 4 [package=1x04-1mm-ra]
  元件9 = Analog Digital MUX Breakout
  JP66 = Header 4 [package=1x04-1mm-ra]
  JP67 = Header 4 [package=1x04-1mm-ra]
  JP68 = Header 4 [package=1x04-1mm-ra]
  JP69 = Header 4 [package=1x04-1mm-ra]
  JP70 = Header 4 [package=1x04-1mm-ra]
  JP71 = Header 4 [package=1x04-1mm-ra]
  JP72 = Header 4 [package=1x04-1mm-ra]
  JP73 = Header 4 [package=1x04-1mm-ra]
  元件10 = Analog Digital MUX Breakout
  JP74 = Header 4 [package=1x04-1mm-ra]
  JP75 = Header 4 [package=1x04-1mm-ra]
  JP76 = Header 4 [package=1x04-1mm-ra]
  JP77 = Header 4 [package=1x04-1mm-ra]
  JP78 = Header 4 [package=1x04-1mm-ra]
  JP79 = Header 4 [package=1x04-1mm-ra]
  JP80 = Header 4 [package=1x04-1mm-ra]
  JP81 = Header 4 [package=1x04-1mm-ra]
  元件11 = Analog Digital MUX Breakout
  JP82 = Header 4 [package=1x04-1mm-ra]
  JP83 = Header 4 [package=1x04-1mm-ra]
  JP84 = Header 4 [package=1x04-1mm-ra]
  JP85 = Header 4 [package=1x04-1mm-ra]
  JP86 = Header 4 [package=1x04-1mm-ra]
  JP87 = Header 4 [package=1x04-1mm-ra]
  JP88 = Header 4 [package=1x04-1mm-ra]
  JP89 = Header 4 [package=1x04-1mm-ra]
  S2 = Round Pushbutton  # not connected
  LED2 = LED - 3mm [color="Red (633nm)" package="3 mm [THT]"]  # not connected
  S3 = Round Pushbutton  # not connected
  LED3 = LED - 3mm [color="Red (633nm)" package="3 mm [THT]"]  # not connected
  S4 = Round Pushbutton  # not connected
  LED4 = LED - 3mm [color="Red (633nm)" package="3 mm [THT]"]  # not connected
  S5 = Round Pushbutton  # not connected
  LED5 = LED - 3mm [color="Red (633nm)" package="3 mm [THT]"]  # not connected
  S6 = Round Pushbutton  # not connected
  LED6 = LED - 3mm [color="Red (633nm)" package="3 mm [THT]"]  # not connected
  S7 = Round Pushbutton  # not connected
  LED7 = LED - 3mm [color="Red (633nm)" package="3 mm [THT]"]  # not connected
  U4 = ENCODER-QUADRATURE [package=encoder-16mm-quad]  # not connected

nets:
  N1: 元件1.C0, JP49.2
  N2: 元件1.C1, JP49.1
  N3: 元件1.C2, JP36.2
  N4: 元件1.C3, JP36.1
  N5: 元件1.C4, JP55.2
  N6: 元件1.C5, JP55.1
  N7: 元件1.C6, JP43.2
  N8: 元件1.C7, JP43.1
  N9: 元件1.C8, JP30.2
  N10: 元件1.C9, JP30.1
  N11: 元件1.C10, JP24.2
  N12: 元件1.C11, JP24.1
  N13: 元件1.C12, JP18.2
  N14: 元件1.C13, JP18.1
  N15: 元件1.C14, JP10.2
  N16: 元件1.C15, JP10.1
  GND: 元件1.GND, 元件2.GND, 元件8.GND, 元件9.GND, 元件10.GND, 元件11.GND
  VCC: 元件1.VCC, 元件2.VCC, 元件8.VCC, 元件9.VCC, 元件10.VCC, 元件11.VCC
  N17: 元件1.EN, U2.Q0
  N18: 元件1.S0, 元件2.S0, U1.Q0, 元件8.S0, 元件9.S0, 元件10.S0, 元件11.S0
  N19: 元件1.S1, 元件2.S1, U1.Q1, 元件8.S1, 元件9.S1, 元件10.S1, 元件11.S1
  N20: 元件1.S2, 元件2.S2, U1.Q2, 元件8.S2, 元件9.S2, 元件10.S2, 元件11.S2
  N21: 元件1.S3, 元件2.S3, U1.Q3, 元件8.S3, 元件9.S3, 元件10.S3, 元件11.S3
  N22: 元件1.SIG, 元件2.SIG, 元件7.A0, 元件8.SIG, 元件9.SIG, 元件10.SIG, 元件11.SIG
  N23: 元件2.C0, JP53.2
  N24: 元件2.C1, JP53.1
  N25: 元件2.C2, JP51.2
  N26: 元件2.C3, JP51.1
  N27: 元件2.C4, JP34.2
  N28: 元件2.C5, JP34.1
  N29: 元件2.C6, JP57.2
  N30: 元件2.C7, JP57.1
  N31: 元件2.C8, JP28.2
  N32: 元件2.C9, JP28.1
  N33: 元件2.C10, JP22.2
  N34: 元件2.C11, JP22.1
  N35: 元件2.C12, JP16.2
  N36: 元件2.C13, JP16.1
  N37: 元件2.C14, JP11.2
  N38: 元件2.C15, JP11.1
  N39: 元件2.EN, U2.Q1
  N40: U1.GND, U2.OE
  N41: U1.Q7', U2.DS
  N42: U1.SH_CP, 元件7.D4
  N43: U1.ST_CP, 元件7.D5_PWM
  N44: U1.OE, 元件7.GND
  N45: U1.DS, 元件7.D3_PWM
  VCC_2: U1.VCC, 元件7.5V
  N46: U2.Q2, 元件8.EN
  N47: U2.Q3, 元件9.EN
  N48: U2.Q4, 元件10.EN
  N49: U2.Q5, 元件11.EN
  N50: JP10.3, JP11.3, JP16.3, JP18.3, JP22.3, JP24.3, JP28.3, JP30.3, JP34.3, JP36.3, JP43.3, JP49.3, JP51.3, JP53.3, JP55.3, JP57.3, JP58.3, JP59.3, JP60.3, JP61.3, JP62.3, JP63.3, JP64.3, JP65.3, JP66.3, JP67.3, JP68.3, JP69.3, JP70.3, JP71.3, JP72.3, JP73.3, JP74.3, JP75.3, JP76.3, JP77.3, JP78.3, JP79.3, JP80.3, JP81.3, JP82.3, JP83.3, JP84.3, JP85.3, JP86.3, JP87.3, JP88.3, JP89.3
  N51: JP10.4, JP11.4, JP16.4, JP18.4, JP22.4, JP24.4, JP28.4, JP30.4, JP34.4, JP36.4, JP43.4, JP49.4, JP51.4, JP53.4, JP55.4, JP57.4, JP58.4, JP59.4, JP60.4, JP61.4, JP62.4, JP63.4, JP64.4, JP65.4, JP66.4, JP67.4, JP68.4, JP69.4, JP70.4, JP71.4, JP72.4, JP73.4, JP74.4, JP75.4, JP76.4, JP77.4, JP78.4, JP79.4, JP80.4, JP81.4, JP82.4, JP83.4, JP84.4, JP85.4, JP86.4, JP87.4, JP88.4, JP89.4
  N52: 元件8.C0, JP59.2
  N53: 元件8.C1, JP59.1
  N54: 元件8.C2, JP61.2
  N55: 元件8.C3, JP61.1
  N56: 元件8.C4, JP60.2
  N57: 元件8.C5, JP60.1
  N58: 元件8.C6, JP58.2
  N59: 元件8.C7, JP58.1
  N60: 元件8.C8, JP64.2
  N61: 元件8.C9, JP64.1
  N62: 元件8.C10, JP65.2
  N63: 元件8.C11, JP65.1
  N64: 元件8.C12, JP62.2
  N65: 元件8.C13, JP62.1
  N66: 元件8.C14, JP63.2
  N67: 元件8.C15, JP63.1
  N68: 元件9.C0, JP67.2
  N69: 元件9.C1, JP67.1
  N70: 元件9.C2, JP69.2
  N71: 元件9.C3, JP69.1
  N72: 元件9.C4, JP68.2
  N73: 元件9.C5, JP68.1
  N74: 元件9.C6, JP66.2
  N75: 元件9.C7, JP66.1
  N76: 元件9.C8, JP72.2
  N77: 元件9.C9, JP72.1
  N78: 元件9.C10, JP73.2
  N79: 元件9.C11, JP73.1
  N80: 元件9.C12, JP70.2
  N81: 元件9.C13, JP70.1
  N82: 元件9.C14, JP71.2
  N83: 元件9.C15, JP71.1
  N84: 元件10.C0, JP75.2
  N85: 元件10.C1, JP75.1
  N86: 元件10.C2, JP77.2
  N87: 元件10.C3, JP77.1
  N88: 元件10.C4, JP76.2
  N89: 元件10.C5, JP76.1
  N90: 元件10.C6, JP74.2
  N91: 元件10.C7, JP74.1
  N92: 元件10.C8, JP80.2
  N93: 元件10.C9, JP80.1
  N94: 元件10.C10, JP81.2
  N95: 元件10.C11, JP81.1
  N96: 元件10.C12, JP78.2
  N97: 元件10.C13, JP78.1
  N98: 元件10.C14, JP79.2
  N99: 元件10.C15, JP79.1
  N100: 元件11.C0, JP83.2
  N101: 元件11.C1, JP83.1
  N102: 元件11.C2, JP85.2
  N103: 元件11.C3, JP85.1
  N104: 元件11.C4, JP84.2
  N105: 元件11.C5, JP84.1
  N106: 元件11.C6, JP82.2
  N107: 元件11.C7, JP82.1
  N108: 元件11.C8, JP88.2
  N109: 元件11.C9, JP88.1
  N110: 元件11.C10, JP89.2
  N111: 元件11.C11, JP89.1
  N112: 元件11.C12, JP86.2
  N113: 元件11.C13, JP86.1
  N114: 元件11.C14, JP87.2
  N115: 元件11.C15, JP87.1
